# Fritzing sketch pi3 (saved by Fritzing 0.9.3b)
breadboards: 1

parts:
  Componente1 = Arduino Uno (Rev3)
  BT1 = Bluetooth HC-06u [package=THT]
  S1 = Round Pushbutton
  R1 = Resistor [tolerance=±5% resistance=2.2k package=THT]
  Q1 = NPN-Transistor [package="TO92 [THT]"]
  R2 = Resistor [tolerance=±20% resistance=860 package=THT]
  J1 = Piezo Speaker
  LED1 = LED - 5mm [color="Red (633nm)" package="5 mm [THT]"]
  LED2 = LED - 5mm [color="Yellow (585nm)" package="5 mm [THT]"]
  LED3 = LED - 5mm [color="Green (555nm)" package="5 mm [THT]"]
  R3 = Resistor [tolerance=±5% resistance=220 package=THT]
  LED4 = LED - 5mm [color="Red (633nm)" package="5 mm [THT]"]
  LED5 = LED - 5mm [color="Green (555nm)" package="5 mm [THT]"]
  R4 = Resistor [tolerance=±5% resistance=220 package=THT]

nets:
  N1: Componente1.D8, LED5.anode
  N2: Componente1.D0/RX, BT1.TXD
  N3: Componente1.D1/TX, BT1.RXD
  N4: Componente1.D2, S1.leg1, R1.Pin_1
  N5: Componente1.D3_PWM, R2.Pin_0
  N6: Componente1.D4, LED1.anode
  N7: Componente1.D5_PWM, LED2.anode
  N8: Componente1.D6_PWM, LED3.anode
  N9: Componente1.D7, LED4.anode
  GND: Componente1.GND, BT1.GND, R1.Pin_0, Q1.E, R3.Pin_0, R4.Pin_0
  VIN: Componente1.VIN, BT1.VCC, S1.leg0, J1.pin2
  N10: Q1.B, R2.Pin_1
  N11: Q1.C, J1.pin1
  N12: LED1.cathode, LED2.cathode, LED3.cathode, R3.Pin_1
  N13: LED4.cathode, LED5.cathode, R4.Pin_1

notes:
  Projeto Integrador 6º Bimestre, 1

custom parts:
  Bluetooth HC-06u: Bluetooth HC-06 - face up, pins down 16.5mm x 37.5mm PCB
